# Fritzing sketch carrier-board (saved by Fritzing 1.0.3b)
breadboards: 1

parts:
  U1 = CH32V203F8U6 [part_number=CH32V203F8U6 package=QFN20]  # not connected
  U2 = ATECC608B CryptoAuthentication Device (I2C, SOIC-8) [part_number=ATECC608B package=SOIC-8]  # not connected
  R1 = Resistor 0603 [resistance=4.7k power=1/10W tolerance=±1% package="[SMD] 0603"]
  R2 = Resistor 0603 [resistance=4.7k power=1/10W tolerance=±1% package="[SMD] 0603"]
  R3 = Resistor 0603 [resistance=10k power=1/10W tolerance=±1% package="[SMD] 0603"]  # not connected
  D1 = LED 0603 [part_number=LED-0603 package="0603 [SMD]"]  # not connected
  BT1 = Supercapacitor 1.5F 5.5V [capacitance=1.5F voltage=5.5V tolerance=-10~+30% package="C型 20.5×7 [THT, supercapacitor]"]  # not connected
  J1 = PIN HEADER 1x4 [part_number=PinHeader-1x4 package=THT]  # not connected
  J2 = PIN HEADER 1x6 [part_number=PinHeader-1x6 package=THT]  # not connected
  J3 = PIN HEADER 1x4 [part_number=PinHeader-1x4 package=THT]  # not connected
  J4 = PIN HEADER 1x7 [part_number=PinHeader-1x7 package=THT]  # not connected

nets:
  N1: R1.1, R2.1

notes:
  图例：

custom parts:
  CH32V203F8U6: WCH CH32V203F8U6 RISC-V MCU, QFN20 3x3 mm / 0.4 mm pitch, 3.3 V, 64K flash / 20K SRAM, 17 I/O, 2x USART (PA9/PA10, PA2/PA3), I2C2 on PB10/PB11, 9+2 ch 12-bit ADC. No NRST / BOOT0 pin (BOOT0 is tied to GND internally) - SWD only, reset by power cycle. Exposed pad = pin 0 / VSS - route to GND.
  Resistor 0603: A generic resistor
  LED 0603: A generic 0603 LED
  Supercapacitor 1.5F 5.5V: Kamcap C-type supercapacitor 1.5F 5.5V (SE-5R5-D155VYC3G)
  PIN HEADER 1x4: 1x4 male pin header, 2.54 mm (0.1 in) pitch, through-hole. Pads are 2.0 mm with a 1.0 mm hole; pin 1 is the square pad.
  PIN HEADER 1x6: 1x6 male pin header, 2.54 mm (0.1 in) pitch, through-hole. Pads are 2.0 mm with a 1.0 mm hole; pin 1 is the square pad.
  PIN HEADER 1x7: 1x7 male pin header, 2.54 mm (0.1 in) pitch, through-hole. Pads are 2.0 mm with a 1.0 mm hole; pin 1 is the square pad.
