# Fritzing sketch carrier-breadboard (saved by Fritzing 1.0.3b)
breadboards: 1

parts:
  U1 = CH32V203F8U6 [part_number=CH32V203F8U6 package=QFN20]
  U2 = ATECC608B CryptoAuthentication Device (I2C, SOIC-8) [part_number=ATECC608B package=SOIC-8]
  R1 = Resistor 0603 [resistance=4.7k power=1/10W tolerance=±1% package="[SMD] 0603"]
  R2 = Resistor 0603 [resistance=4.7k power=1/10W tolerance=±1% package="[SMD] 0603"]
  R3 = Resistor 0603 [resistance=10k power=1/10W tolerance=±1% package="[SMD] 0603"]
  D1 = LED 0603 [part_number=LED-0603 package="0603 [SMD]"]
  BT1 = Supercapacitor 1.5F 5.5V [capacitance=1.5F voltage=5.5V tolerance=-10~+30% part_number=SE-5R5-D155VYC3G package="C型 20.5×7 [THT, supercapacitor]"]
  J1 = PIN HEADER 1x4 [part_number=PinHeader-1x4 form="♂ (male)" package=THT]
  J2 = PIN HEADER 1x6 [part_number=PinHeader-1x6 form="♂ (male)" package=THT]
  J3 = PIN HEADER 1x4 [part_number=PinHeader-1x4 form="♂ (male)" package=THT]
  J4 = PIN HEADER 1x7 [part_number=PinHeader-1x7 form="♂ (male)" package=THT]
  SW1 = SK-12D02VG3 [part_number=SK-12D02VG3]

nets:
  N1: U1.PA0/WKUP, J4.5
  N2: U1.PA2/USART2_TX, J1.3
  N3: U1.PA3/USART2_RX, J1.4
  N4: U1.PB0/ADC8, D1.C
  N5: U1.PB10/I2C2_SCL, U2.SCL, R1.2, J2.4
  N6: U1.PB11/I2C2_SDA, U2.SDA, R2.2, J2.3
  N7: U1.PA9/USART1_TX, J2.5
  N8: U1.PA13/SWD, J3.3
  N9: U1.PA14/SWC, J3.4
  N10: U1.PA10/USART1_RX, J2.6
  VDD: U1.VDD, U2.VCC, R1.1, R2.1, R3.1, J1.1, J2.1, J3.1, SW1.connector0
  VSS: U1.VSS, U2.GND, BT1.-, J1.2, J2.2, J3.2, J4.2
  N11: R3.2, D1.A
  N12: BT1.+, J4.3
  N13: J4.4, J4.6, J4.7, SW1.connector1

notes:
  图例：
  GND
  3V3
  VBAT
  VBUS_IN
  VBAT_OK
  SDA
  SCL
  MOD_RX
  MOD_TX
  CON_TX
  CON_RX
  SWDIO
  SWCLK
  LED_R
  LED_HB

custom parts:
  CH32V203F8U6: WCH CH32V203F8U6 RISC-V MCU, QFN20 3x3 mm / 0.4 mm pitch, 3.3 V, 64K flash / 20K SRAM, 17 I/O, 2x USART (PA9/PA10, PA2/PA3), I2C2 on PB10/PB11, 9+2 ch 12-bit ADC. No NRST / BOOT0 pin (BOOT0 is tied to GND internally) - SWD only, reset by power cycle. Exposed pad = pin 0 / VSS - route to GND.
  Resistor 0603: A generic resistor
  LED 0603: A generic 0603 LED
  Supercapacitor 1.5F 5.5V: Kamcap C-type supercapacitor 1.5F 5.5V (SE-5R5-D155VYC3G)
  PIN HEADER 1x4: 1x4 male pin header, 2.54 mm (0.1 in) pitch, through-hole. Pads are 2.0 mm with a 1.0 mm hole; pin 1 is the square pad.
  PIN HEADER 1x6: 1x6 male pin header, 2.54 mm (0.1 in) pitch, through-hole. Pads are 2.0 mm with a 1.0 mm hole; pin 1 is the square pad.
  PIN HEADER 1x7: 1x7 male pin header, 2.54 mm (0.1 in) pitch, through-hole. Pads are 2.0 mm with a 1.0 mm hole; pin 1 is the square pad.
