# Fritzing sketch carrier-schematic (saved by Fritzing 1.0.3b)

parts:
  U1 = CH32V203F8U6 [part_number=CH32V203F8U6 package=QFN20]
  U2 = ATECC608B CryptoAuthentication Device (I2C, SOIC-8) [part_number=ATECC608B package=SOIC-8]
  R1 = Resistor 0603 [part_number=R0603_36137a0f26fc46e91e48eb74468f61a7_1 package="[SMD] 0603"]
  R2 = Resistor 0603 [part_number=R0603_36137a0f26fc46e91e48eb74468f61a7_1 package="[SMD] 0603"]
  R3 = Resistor 0603 [part_number=R0603_36137a0f26fc46e91e48eb74468f61a7_1 package="[SMD] 0603"]
  D1 = LEDs [part_number=SparkFun-LED-LED-0603 package=led-0603]
  BT1 = Electrolytic Capacitor [part_number=capacitor_elko_goldcap_4.0F_92eef0d1d2f548b9db9918a1769107d3_2 package="2cm H-Type"]
  J1 = PIN HEADER 1x4 [part_number=PinHeader-1x4 package=THT]
  J2 = PIN HEADER 1x6 [part_number=PinHeader-1x6 package=THT]
  J3 = PIN HEADER 1x4 [part_number=PinHeader-1x4 package=THT]
  J4 = PIN HEADER 1x7 [part_number=PinHeader-1x7 package=THT]

nets:
  N1: U1.PA0/WKUP, J4.5
  N2: U1.PA2/USART2_TX, J1.3
  N3: U1.PA3/USART2_RX, J1.4
  N4: U1.PB0/ADC8, D1.C
  N5: U1.PB10/I2C2_SCL, U2.SCL, R1.2, J2.4
  N6: U1.PB11/I2C2_SDA, U2.SDA, R2.2, J2.3
  N7: U1.PA9/USART1_TX, J2.5
  N8: U1.PA13/SWD, J3.3
  N9: U1.PA14/SWC, J3.4
  N10: U1.PA10/USART1_RX, J2.6
  VDD: U1.VDD, U2.VCC, R1.1, R2.1, R3.1, J1.1, J2.1, J3.1, J4.4, J4.6, J4.7
  VSS: U1.VSS, U2.GND, BT1.+, J1.2, J2.2, J3.2, J4.2
  N11: R3.2, D1.A
  N12: BT1.-, J4.3

custom parts:
  CH32V203F8U6: WCH CH32V203F8U6 RISC-V MCU, QFN20 3x3 mm / 0.4 mm pitch, 3.3 V, 64K flash / 20K SRAM, 17 I/O, 2x USART (PA9/PA10, PA2/PA3), I2C2 on PB10/PB11, 9+2 ch 12-bit ADC. No NRST / BOOT0 pin (BOOT0 is tied to GND internally) - SWD only, reset by power cycle. Exposed pad = pin 0 / VSS - route to GND.
  Resistor 0603: A generic resistor
  PIN HEADER 1x4: 1x4 male pin header, 2.54 mm (0.1 in) pitch, through-hole. Pads are 2.0 mm with a 1.0 mm hole; pin 1 is the square pad.
  PIN HEADER 1x6: 1x6 male pin header, 2.54 mm (0.1 in) pitch, through-hole. Pads are 2.0 mm with a 1.0 mm hole; pin 1 is the square pad.
  PIN HEADER 1x7: 1x7 male pin header, 2.54 mm (0.1 in) pitch, through-hole. Pads are 2.0 mm with a 1.0 mm hole; pin 1 is the square pad.
