# Fritzing sketch bstep-ch347f-2txah-evb (saved by Fritzing 1.0.3b)

parts:
  U2 = TX-AH-R900PNR (Taixin 802.11ah Module) rev.1 [package=TX-AH-R900PNR]
  U3 = CH347F (USB to SPI/I2C/JTAG/UART, QFN28) [package=QFN28]
  U4 = TX-AH-R900PNR (Taixin 802.11ah Module) rev.1 [package=TX-AH-R900PNR]

nets:
  GND: U2.GND, U3.GND, U4.GND
  N1: U2.A11, U3.RXD0
  N2: U2.A13, U2.CH340E_RX
  N3: U2.A10, U3.TXD0
  N4: U2.A12, U2.CH340E_TX
  N5: U3.TXD1, U4.A10
  N6: U3.RXD1, U4.A11
  N7: U4.A13, U4.CH340E_RX
  N8: U4.A12, U4.CH340E_TX
