# Fritzing sketch bstep-ch347f-txah-evb-thrj45 (saved by Fritzing 1.0.3b)

parts:
  U3 = CH347F (USB to SPI/I2C/JTAG/UART, QFN28) [package=QFN28]
  U5 = TX-AH-R900PNR (Taixin 802.11ah Module) [package=TX-AH-R900PNR]

nets:
  N1: U3.TXD0, U5.A10
  N2: U3.RXD0, U5.A11
  GND: U3.GND, U5.GND
