# Fritzing sketch bstep-ch347f-txah-evb (saved by Fritzing 1.0.3b)

parts:
  U2 = TX-AH-R900PNR (Taixin 802.11ah Module) rev.1 [package=TX-AH-R900PNR]
  U3 = CH347F (USB to SPI/I2C/JTAG/UART, QFN28) [package=QFN28]

nets:
  GND: U2.GND, U3.GND
  N1: U2.A11, U3.RXD0
  N2: U2.A13, U3.RXD1
  N3: U2.A10, U3.TXD0
  N4: U2.A12, U3.TXD1
  N5: U2.VCC, U3.VIO
