# Fritzing sketch cstep-ch347f-atecc608b (saved by Fritzing 1.0.3b)
breadboards: 1

parts:
  U3 = CH347F (USB to SPI/I2C/JTAG/UART, QFN28) [package=QFN28]
  U5 = ATECC608B CryptoAuthentication Device (I2C, SOIC-8) [part_number=ATECC608B package=SOIC-8]
  R1 = Resistor [tolerance=±5% power=0.25W resistance=4.7k package=THT]
  R2 = Resistor [tolerance=±5% power=0.25W resistance=4.7k package=THT]

nets:
  N1: U3.SDA, U5.SDA, R1.Pin_1
  N2: U3.SCL, U5.SCL, R2.Pin_1
  3V3: U3.3V3, U5.VCC, R1.Pin_0, R2.Pin_0
  GND: U3.GND, U5.GND
