# Fritzing sketch cstep-ch347f-nanoch32-atecc608b (saved by Fritzing 1.0.3b)
breadboards: 1

parts:
  U5 = ATECC608B CryptoAuthentication Device (I2C, SOIC-8) [part_number=ATECC608B package=SOIC-8]
  R1 = Resistor [tolerance=±5% power=0.25W resistance=4.7k package=THT]
  R2 = Resistor [tolerance=±5% power=0.25W resistance=4.7k package=THT]
  U6 = nanoCH32V203 (CH32V203C8T6 dev board) [package=LQFP48]
  U7 = CH347F (USB to SPI/I2C/JTAG/UART, QFN28) [package=QFN28]

nets:
  GND: U5.GND, U6.VSS_1, U6.VSS_2, U6.VSS_3, U7.GND
  N1: U5.SDA, R1.Pin_1, U6.PB7/USB2DM
  N2: U5.SCL, R2.Pin_1, U6.PB6/USB2DP
  N3: U5.VCC, R1.Pin_0, R2.Pin_0, U6.VDDA, U6.VDD_VIO_1, U6.VDD_2
  N4: U6.PA9, U7.RXD0
  N5: U6.PA10, U7.TXD0
