# Fritzing sketch cstep-ch347f-nanoch32-i2ctest (saved by Fritzing 1.0.3b)
breadboards: 1

parts:
  U6 = nanoCH32V203 (CH32V203C8T6 dev board) [package=LQFP48]
  U7 = CH347F (USB to SPI/I2C/JTAG/UART, QFN28) [package=QFN28]
  R2 = Resistor [tolerance=±5% power=0.25W resistance=4.7k package=THT]
  R1 = Resistor [tolerance=±5% power=0.25W resistance=4.7k package=THT]

nets:
  N1: U6.PA9, U7.RXD0
  N2: U6.PA10, U7.TXD0
  N3: U6.PB6/USB2DP, U7.SCL, R2.Pin_0
  N4: U6.PB7/USB2DM, U7.SDA, R1.Pin_0
  GND: U6.GND, U7.GND
  N5: U7.3V3, R2.Pin_1, R1.Pin_1
