# Fritzing sketch cstep-ch347f-txah-evb-nanoch32-atecc608b (saved by Fritzing 1.0.3b)
breadboards: 1

parts:
  U2 = TX-AH-R900PNR (Taixin 802.11ah Module) rev.1 [package=TX-AH-R900PNR]
  U3 = CH347F (USB to SPI/I2C/JTAG/UART, QFN28) [package=QFN28]
  U4 = nanoCH32V203 (CH32V203C8T6 dev board) [package=LQFP48]
  U5 = ATECC608B CryptoAuthentication Device (I2C, SOIC-8) [part_number=ATECC608B package=SOIC-8]
  R1 = Resistor [tolerance=±5% power=0.25W resistance=4.7k package=THT]
  R2 = Resistor [tolerance=±5% power=0.25W resistance=4.7k package=THT]

nets:
  GND: U2.GND, U3.GND, U4.VSSA, U4.VSS_2, U4.GND, U5.GND
  N1: U2.A11, U4.PA3/ADC3
  N2: U2.A10, U4.PA2/ADC2
  N3: U2.A13, U3.RXD1
  N4: U2.A12, U3.TXD1
  N5: U3.TXD0, U4.PA10
  N6: U3.RXD0, U4.PA9
  N7: U4.VDDA, U4.VDD_VIO_1, U4.VDD_2, U5.VCC, R1.Pin_0, R2.Pin_0
  N8: U4.PB6/USB2DP, U5.SCL, R2.Pin_1
  N9: U4.PB7/USB2DM, U5.SDA, R1.Pin_1
