# Fritzing sketch cstep-ch347f-txah-evb-nanoch32 (saved by Fritzing 1.0.3b)

parts:
  U2 = TX-AH-R900PNR (Taixin 802.11ah Module) rev.1 [package=TX-AH-R900PNR]
  U3 = CH347F (USB to SPI/I2C/JTAG/UART, QFN28) [package=QFN28]
  U4 = nanoCH32V203 (CH32V203C8T6 dev board) [package=LQFP48]

nets:
  GND: U2.GND, U3.GND, U4.GND
  N1: U2.A11, U4.PA3/ADC3
  N2: U2.A10, U4.PA2/ADC2
  N3: U2.A13, U3.RXD1
  N4: U2.A12, U3.TXD1
  N5: U3.TXD0, U4.PA10
  N6: U3.RXD0, U4.PA9
