# Fritzing sketch cstep-nanoch32-atecc608b (saved by Fritzing 1.0.3b)
breadboards: 1

parts:
  U5 = ATECC608B CryptoAuthentication Device (I2C, SOIC-8) [part_number=ATECC608B package=SOIC-8]
  R1 = Resistor [tolerance=±5% power=0.25W resistance=4.7k package=THT]
  R2 = Resistor [tolerance=±5% power=0.25W resistance=4.7k package=THT]
  U6 = nanoCH32V203 (CH32V203C8T6 dev board) [package=LQFP48]

nets:
  N1: U5.GND, U6.VSS_1, U6.VSS_2
  N2: U5.SDA, R1.Pin_1, U6.PB7/USB2DM
  N3: U5.SCL, R2.Pin_1, U6.PB6/USB2DP
  N4: U5.VCC, R1.Pin_0, R2.Pin_0, U6.VDDA, U6.VDD_VIO_1, U6.VDD_2
